# Fritzing sketch Schema_CMG001A (saved by Fritzing 0.8.3b)
breadboards: 1

parts:
  Componente1 = Arduino Uno (Rev3)
  LCD1 = Adafruit Negative RGB 2x16 LCD
  kEYPAD_MATRICIAL_1 = KEYPAD 4x3
  J1 = Piezo Speaker
  K1 = Relay [part_number=FRS1B-S package=THT]
  S1 = Toggle Switch [package=THT]
  TRS1 = Audio Jack (TRS) 3.5mm [package="4Ucon 08780 [THT]"]
  R1 = Trimmer Potentiometer [maximum_resistance=10kΩ package=THT]
  S2 = Round Pushbutton
  R2 = Trimmer Potentiometer [maximum_resistance=10kΩ package=THT]
  R4 = Resistor [tolerance=±5% resistance=10k package=THT]
  R5 = Resistor [tolerance=±5% resistance=330 package=THT]
  S3 = Toggle Switch [package=THT]

nets:
  N1: Componente1.A0, kEYPAD_MATRICIAL_1.col1
  N2: Componente1.A1, kEYPAD_MATRICIAL_1.arrow1
  N3: Componente1.A2, kEYPAD_MATRICIAL_1.col2
  N4: Componente1.A3, kEYPAD_MATRICIAL_1.arrow2
  N5: Componente1.A4/SDA, kEYPAD_MATRICIAL_1.col3
  N6: Componente1.A5/SCL, kEYPAD_MATRICIAL_1.arrow3
  N7: Componente1.ICSP_MOSI, Componente1.D11_PWM/MOSI, Componente1.D12/MISO, kEYPAD_MATRICIAL_1.arrow4
  N8: Componente1.GND, LCD1.no_name_yet#100, LCD1.no_name_yet#104, J1.pin1, K1.COIL1, S1.L2, R1.leg1, R2.leg1
  N9: Componente1.D8, S3.COM
  N10: Componente1.D9_PWM, R5.Pin_1
  N11: Componente1.D10_PWM/SS, K1.C1, K1.C2
  N12: Componente1.D13/SCK, R4.Pin_0
  N13: Componente1.D2, LCD1.no_name_yet#103
  N14: Componente1.D3_PWM, LCD1.no_name_yet#105
  N15: Componente1.D4, LCD1.no_name_yet#110
  N16: Componente1.D5_PWM, LCD1.no_name_yet#111
  N17: Componente1.D6_PWM, LCD1.no_name_yet#112
  N18: Componente1.D7, LCD1.no_name_yet#113
  N19: Componente1.5V, LCD1.no_name_yet#101, LCD1.no_name_yet#114, K1.COIL2, S1.L1, TRS1.Sleeve, R1.leg2, S2.leg1, R2.leg2
  N20: LCD1.no_name_yet#102, R1.wiper
  N21: LCD1.no_name_yet#115, R2.wiper
  N22: J1.pin2, S3.L1, S3.L2
  N23: S1.COM, R5.Pin_0
  N24: TRS1.Ring, TRS1.Tip, S2.leg0, R4.Pin_1

notes:
  JACK mono 1/4" female for pedal
  This should be a 4x4 keypad, if only Fritzing had the model
  the ORANGE pot. controls the backlight, the YELLOW one controls the LCD contrast

custom parts:
  Adafruit Negative RGB 2x16 LCD: Adafruit Negative 2x16 LCD Display with RGB Backlight
  KEYPAD 4x3: KEYPAD matricial de 12 botones, 4 filas x 3 columnas
