# Fritzing sketch Schema_DL002A (saved by Fritzing 0.7.11b)
breadboards: 1

parts:
  kEYPAD_MATRICIAL_1 = KEYPAD 4x3
  J1 = Piezo Speaker
  K1 = Relay [part_number=FRS1B-S package=THT]
  S1 = Toggle Switch [package=THT]
  TRS1 = Audio Jack (TRS) 3.5mm [package="4Ucon 08780 [THT]"]
  S2 = Round Pushbutton
  R4 = Resistor [tolerance=±5% resistance=10k package=THT]
  7_Segment1 = 7 Segment Display
  7_Segment2 = 7 Segment Display  # not connected
  7_Segment3 = 7 Segment Display  # not connected
  7_Segment4 = 7 Segment Display
  7_Segment5 = 7 Segment Display
  Arduino1 = Arduino
  R7 = Resistor [tolerance=±5% resistance=330 package=THT]
  R8 = Rotary Potentiometer (Small) [maximum_resistance=100kΩ]
  R6 = Rotary Potentiometer (Small) [maximum_resistance=100kΩ]

nets:
  N1: kEYPAD_MATRICIAL_1.col1, Arduino1.D2
  N2: kEYPAD_MATRICIAL_1.arrow1, Arduino1.D3
  N3: kEYPAD_MATRICIAL_1.col2, Arduino1.D4
  N4: kEYPAD_MATRICIAL_1.arrow2, Arduino1.D5
  N5: kEYPAD_MATRICIAL_1.col3, Arduino1.D6
  N6: kEYPAD_MATRICIAL_1.arrow3, Arduino1.D7
  N7: kEYPAD_MATRICIAL_1.arrow4, Arduino1.D8
  N8: J1.pin1, K1.COIL1, S1.L2, 7_Segment1.Segment_E, 7_Segment4.Segment_C, Arduino1.GND, R8.leg1
  N9: J1.pin2, R6.leg2
  N10: K1.C1, K1.C2, Arduino1.D11
  N11: K1.COIL2, S1.L1, TRS1.Sleeve, S2.leg1, 7_Segment1.Segment_D, 7_Segment4.Segment_DP, Arduino1.+5V, R8.leg2
  N12: TRS1.Ring, TRS1.Tip, S2.leg0, R4.Pin_1
  N13: R4.Pin_0, Arduino1.D13
  N14: 7_Segment4.Segment_B, Arduino1.A1
  N15: 7_Segment4.Segment_A, Arduino1.A0
  N16: 7_Segment5.Segment_C, Arduino1.A2
  N17: Arduino1.D12, R6.leg1
  N18: Arduino1.D10, R7.Pin_1
  N19: Arduino1.A3, R8.wiper

notes:
  JACK mono 1/4" female for pedal
  This should be a 4x4 keypad, if only Fritzing had the model
  Grove LED Bar (serial)
  http://www.seeedstudio.com/wiki/Grove_-_LED_Bar
  wire DI to pin A0
  and DCKI to pin A1
  Sparkfun 7-Segment Serial Display
  https://www.sparkfun.com/products/11441
  Wire RX to pin A2,
  GND and VCC as usual.

custom parts:
  KEYPAD 4x3: KEYPAD matricial de 12 botones, 4 filas x 3 columnas
